# Fritzing sketch marv (saved by Fritzing 0.9.3b)
breadboards: 1

parts:
  Part1 = Arduino Uno (Rev3)
  Raspberry_Pi_1 = Raspberry Pi 3 [part_number=RPI-3-V1.2]
  Part5 = 9-DOF Absolute Orientation IMU Fusion Breakout - BNO055  # not connected
  U2 = LIPO-2000mAh [package=lipo-2000]
  Part6 = PowerBoost 1000 Basic
  Part2 = 16-Channel 12-bit PWM Servo Driver - I2C [part_number=815]
  J1 = Basic Servo  # not connected
  J2 = Basic Servo  # not connected

nets:
  VIN: Part1.VIN, Raspberry_Pi_1.5V, Part6.5.0V
  3V3: Raspberry_Pi_1.3v3, Raspberry_Pi_1.3V3, Part2.VCC
  N1: Raspberry_Pi_1.GPIO2, Part2.SDA
  N2: Raspberry_Pi_1.GPIO3, Part2.SCL
  GND: Raspberry_Pi_1.GND, U2.-, Part6.GND, Part2.GND
  N3: U2.+, Part6.VBAT

custom parts:
  9-DOF Absolute Orientation IMU Fusion Breakout - BNO055: A MEMS accelerometer, magnetometer and gyroscope on a single die with a high speed ARM Cortex-M0 based processor to digest all the sensor data, abstract the sensor fusion and real time requirements away, and spit out data you can use in quaternions, Euler angles or vectors.
  PowerBoost 1000 Basic: The PowerBoost 1000 is a little DC/DC boost converter module that can run from 1.8V batteries or higher, and convert the battery output to 5.2V DC for running your 5V projects. At its heart is a TPS61030 boost converter from TI. This boost converter chip has some really nice extras such as low battery detection, 4A internal switch, synchronous conversion, excellent efficiency, and 700KHz high-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
  16-Channel 12-bit PWM Servo Driver - I2C: You want to make a cool robot, maybe a hexapod walker, or maybe just a piece of art with a lot of moving parts. Or maybe you want to drive a lot of LEDs with precise PWM output. Using only two pins, control 16 free-running PWM outputs! You can even chain up 62 breakouts to control up to 992 PWM outputs.
